// Logisim project CLAA.circ as structural Verilog: 1 circuit, main circuit CLAA
module CLAA (
  input  B3,
  input  A3,
  input  B2,
  input  A2,
  input  B1,
  input  A1,
  input  B0,
  input  A0,
  input  Cin,
  output Cout,
  output S3,
  output S2,
  output S1,
  output S0
);

  wire and_1_out, and_2_out, and_3_out, and_4_out, circuitopg_1_c1, circuitopg_1_c2, circuitopg_1_c3,
       xor_1_out, xor_2_out, xor_3_out, xor_4_out;

  xor xor_1 (xor_1_out, B3, A3);
  and and_1 (and_1_out, B3, A3);
  xor xor_2 (xor_2_out, B2, A2);
  and and_2 (and_2_out, B2, A2);
  xor xor_3 (xor_3_out, B1, A1);
  and and_3 (and_3_out, B1, A1);
  xor xor_4 (xor_4_out, B0, A0);
  and and_4 (and_4_out, B0, A0);
  circuitoPG circuitopg_1 (
    .P3(xor_1_out), .G3(and_1_out), .P2(xor_2_out), .G2(and_2_out), .P1(xor_3_out), .G1(and_3_out),
    .P0(xor_4_out), .G0(and_4_out), .C0(Cin), .C4(Cout), .C3(circuitopg_1_c3), .C2(circuitopg_1_c2),
    .C1(circuitopg_1_c1));
  xor xor_5 (S3, xor_1_out, circuitopg_1_c3);
  xor xor_6 (S2, xor_2_out, circuitopg_1_c2);
  xor xor_7 (S1, xor_3_out, circuitopg_1_c1);
  xor xor_8 (S0, xor_4_out, Cin);

  // Notes on the sheet:
  //   ENTRADAS
  //   SALIDAS
endmodule
